# Fritzing sketch sketch (saved by Fritzing 0.9.2b)
breadboards: 2

parts:
  Raspberry_Pi1 = Raspberry Pi 2
  RHT1 = Humidity and Temperature Sensor RHT03
  LCD1 = LCD screen
  U1 = POT [package=pot_mammoth]
  U3 = POT [package=pot_alpha_rv16af-20]
  Raspberry_Pi2 = Raspberry Pi 2
  RHT2 = Humidity and Temperature Sensor RHT03
  LCD2 = LCD screen
  U4 = POT [package=pot_mammoth]
  U5 = POT [package=pot_alpha_rv16af-20]
  U10 = RELAY-SOLIDSTATE [package=relay-s108t02]
  U11 = RELAY-SOLIDSTATE [package=relay-s108t02]
  LED1 = LED - 3mm [color="Red (633nm)" package="3 mm [THT]"]
  LED2 = LED - 3mm [color="Red (633nm)" package="3 mm [THT]"]
  LED3 = LED - 3mm [color="Red (633nm)" package="3 mm [THT]"]  # not connected
  R1 = Resistor [tolerance=±5% resistance=220 package=THT]

nets:
  N1: Raspberry_Pi1.GIPO11, LCD1.DB7
  N2: Raspberry_Pi1.GIPO5, LCD1.DB6
  N3: Raspberry_Pi1.GIPO6, LCD1.DB5
  N4: Raspberry_Pi1.GIPO13, LCD1.DB4
  N5: Raspberry_Pi1.GIPO26, LCD1.RS
  GND: Raspberry_Pi1.GND, RHT1.Data-signal, RHT1.GND_2, LCD1.VSS, LCD1.R/W, LCD1.E, LCD1.LED-, U1.S
  5V: Raspberry_Pi1.5V, RHT1.GND_1, LCD1.VDD, U3.A
  N6: LCD1.V0, U1.A
  N7: LCD1.LED+, U3.S
  N8: Raspberry_Pi2.GIPO4, RHT2.Data-signal
  N9: Raspberry_Pi2.GIPO11, Raspberry_Pi2.GIPO8, LCD2.DB7
  GND_2: Raspberry_Pi2.GIPO5, Raspberry_Pi2.GIPO13, Raspberry_Pi2.GND, RHT2.GND_2, LCD2.VSS, LCD2.R/W, LCD2.DB4, LCD2.DB6, LCD2.LED-
  N10: Raspberry_Pi2.GIPO6, Raspberry_Pi2.GIPO12, LCD2.DB5
  N11: Raspberry_Pi2.GIPO19, Raspberry_Pi2.GIPO16, LCD2.E
  N12: Raspberry_Pi2.GIPO26, Raspberry_Pi2.GIPO20, LCD2.RS
  N13: Raspberry_Pi2.GIPO15, U11.+
  N14: Raspberry_Pi2.GIPO14, U10.+
  5V_2: Raspberry_Pi2.5V, RHT2.GND_1, LCD2.VDD
  N15: LCD2.V0, U4.A
  N16: LCD2.LED+, U5.S
  N17: U4.S, U10.-, U11.-
  N18: U10.T1, LED2.cathode
  N19: U10.T2, LED2.anode
  N20: U11.T1, R1.Pin_1
  N21: U11.T2, LED1.anode
  N22: LED1.cathode, R1.Pin_0
